# Fritzing sketch rasp-01 (saved by Fritzing 0.9.3b)
breadboards: 1

parts:
  MCU1 = Raspberry Pi Zero
  DHT1 = DHT22 Humidity and Temperature Sensor
  LED1 = LED - 3mm [color="Green (565nm)" package="3 mm [THT]"]
  R2 = Resistor [tolerance=±2% resistance=10k package=THT]
  R3 = Resistor [tolerance=±5% resistance=10k package=THT]

nets:
  N1: MCU1.pin_1, MCU1.pin_17, DHT1.VDD, DHT1.DATA, R3.Pin_0
  N2: MCU1.pin_6, DHT1.GND, R2.Pin_1
  N3: MCU1.pin_13, R3.Pin_1
  N4: LED1.anode, R2.Pin_0
