# Fritzing sketch rasp-02 (saved by Fritzing 0.9.3b)
breadboards: 1

parts:
  MCU1 = Raspberry Pi Zero
  LED1 = LED - 3mm [color="Green (565nm)" package="3 mm [THT]"]
  IC1 = MCP3008 8-channel 10-bit ADC [part_number=MCP3008]
  R1 = Temperature Sensor (Thermistor) [thermistor_type=NTC package=THT]
  R2 = Photocell (LDR) [package=THT]
  R3 = Resistor [tolerance=±5% resistance=10k package=THT]
  R4 = Resistor [tolerance=±5% resistance=10k package=THT]
  R5 = Resistor [tolerance=±5% resistance=100k package=THT]

nets:
  N1: MCU1.pin_1, IC1.no_name_yet#15
  N2: MCU1.pin_6, MCU1.pin_9, MCU1.pin_30, MCU1.pin_34, MCU1.pin_39, IC1.no_name_yet#9, IC1.no_name_yet#14, R3.Pin_0, R4.Pin_0, R5.Pin_0
  N3: MCU1.pin_11, LED1.cathode
  N4: MCU1.pin_19, IC1.no_name_yet#11
  N5: MCU1.pin_21, IC1.no_name_yet#12
  N6: MCU1.pin_23, IC1.no_name_yet#13
  N7: MCU1.pin_24, IC1.no_name_yet#10
  N8: LED1.anode, R5.Pin_1
  N9: IC1.no_name_yet#1, R1.pin_0, R3.Pin_1
  N10: IC1.no_name_yet#2, R2.pin_0, R4.Pin_1
